# Fritzing sketch sensor (saved by Fritzing 0.9.2b)
breadboards: 1

parts:
  BeagleBone1 = BeagleBone Black
  SONAR1 = Maxbotix MaxSonar Ultrasonic Sensor
  U1 = QRD1114 [package=qrd1114]

nets:
  N1: BeagleBone1.no_name_yet#1, SONAR1.GND, U1.C, U1.K
  N2: BeagleBone1.no_name_yet#3, SONAR1.+5V, U1.A
  N3: BeagleBone1.no_name_yet#33, U1.E
  N4: BeagleBone1.no_name_yet#36, SONAR1.AN

custom parts:
  BeagleBone Black: BeagleBone Black rev. A5B
  Maxbotix MaxSonar Ultrasonic Sensor: Maxbotix MaxSonar Ultrasonic Sensor LV-EZ0, LV-EZ1, LV-EZ2, LV-EZ3, LV-EZ4
