# Fritzing sketch Lab07 (saved by Fritzing 0.9.2b)
breadboards: 1

parts:
  BeagleBone1 = BeagleBone Black
  GY1 = MPU-6050 Board GY-521 [form="♀ (female)" package=THT]

nets:
  N1: BeagleBone1.no_name_yet#1, GY1.pin2
  N2: BeagleBone1.no_name_yet#3, GY1.pin1
  N3: BeagleBone1.no_name_yet#17, GY1.pin3
  N4: BeagleBone1.no_name_yet#18, GY1.pin4

custom parts:
  BeagleBone Black: BeagleBone Black rev. A5B
  MPU-6050 Board GY-521: Acelerometro y Giroscopio MPU-6050 Board GY-521
